# Fritzing sketch Full Control board+ pressure sensor wiring (saved by Fritzing 0.8.7b)
stripboards: 2

parts:
  Part1 = Arduino Uno (Rev3)
  Part2 = LCD1602-I2C
  R1 = Rotary Potentiometer (Small) [maximum_resistance=100kΩ package=THT]
  R2 = Rotary Potentiometer (Small) [maximum_resistance=100kΩ package=THT]
  R3 = Rotary Potentiometer (Small) [maximum_resistance=100kΩ package=THT]
  M1 = Stepper Motor - Bipolar
  M2 = Stepper Motor - Bipolar
  M4 = Stepper Motor - Bipolar
  D2F1 = D2F-FL Omron Snap Action Limit Switch with Level
  D2F2 = D2F-FL Omron Snap Action Limit Switch with Level
  S1 = Round Pushbutton
  S2 = Round Pushbutton
  VCC1 = Battery block 9V
  M5 = Stepper Motor - Bipolar
  R4 = Resistor [package="2010 [SMD]"]
  R6 = Resistor [package="2010 [SMD]"]
  MPX1 = MPX2010 pressure sensor [part_number=MPX]

nets:
  N1: Part1.A0, MPX1.GND
  N2: Part1.A1, R1.wiper
  N3: Part1.A2, R2.wiper
  N4: Part1.A3, R3.wiper
  N5: Part1.D8, Part2.GND, D2F2.NO, R6.Pin_0, R6.Pin_1
  N6: Part1.D13/SCK, S1.leg1
  N7: Part1.A4/SDA, Part2.SDA
  N8: Part1.A5/SCL, Part2.SCL
  N9: Part1.D2, Part1.D3_PWM, M2.B, M2.D, M4.B, M4.D
  N10: Part1.D4, Part1.D5_PWM, M1.B, M1.D, M5.B, M5.D
  N11: Part1.D7, Part1.GND, D2F1.NO, R4.Pin_0, R4.Pin_1
  5V: Part1.5V, Part2.VCC, R1.leg1, R2.leg1, R3.leg1, D2F1.COM, D2F2.COM, S1.leg0, MPX1.Vs
  N12: M1.A, M5.A
  N13: M1.C, M5.C
  N14: M2.A, M4.A
  N15: M2.C, M4.C
  N16: S2.leg0, VCC1.-
  N17: S2.leg1, VCC1.+

notes:
  VCC__GND____A+___A-___B+___B-___PUL+___PUL-___DIR+___DIR-
  RED- (POWER 30V/5A)
  BLACK- (GROUND)
  YELLOW- (PUL +)
  BLUE- (DIR+)
  PURPLE- (INFO Pin)
  GREEN- (SDA Pin)
  ORANGE- (SLC Pin)
  Keep In Mind that this Pressure sensor is used for wiring purpose, the original one used in the prototype is MPX5010DP.

custom parts:
  LCD1602-I2C: A standard character display, usually with 2x16 characters. Comes in many colors with LCM1602 IIC attached.
  D2F-FL Omron Snap Action Limit Switch with Level: Snap action switch with stainless steel lever.
